# Fritzing sketch ESp32withMPU6050 (saved by Fritzing 0.9.3b)
breadboards: 2

parts:
  M1 = DOIT Esp32 DevKit v1 (30 pins long, 11 pins width) [part_number=ESP32S-PIN30]
  Part1 = InvenSense MPU6050
  VCC1 = Battery block 9V

nets:
  3V3: M1.3V3, Part1.VCC
  GND: M1.GND, Part1.GND, VCC1.-
  N1: M1.D21, Part1.SDA
  N2: M1.D22, Part1.SCL
  N3: M1.VIN, VCC1.+

custom parts:
  DOIT Esp32 DevKit v1 (30 pins long, 11 pins width): The DOIT Esp32 DevKit v1 is one of the development board created by DOIT to evaluate the ESP-WROOM-32 module. It is based on the ESP32 microcontroller that boasts Wifi, Bluetooth, Ethernet and Low Power support all in a single chip. (vanepp) made breadboard work, adjusted pin numbering and labels and reduced size of schematic and cleaned up pcb. This chip is 30pins long (2 x15) and 11 pins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
