# Fritzing sketch ESPSR Schematic (saved by Fritzing 0.9.3b)
breadboards: 1

parts:
  M1 = ESP32-S3-DevKitC-1-N8R8-v1 [part_number=ESP32-S3-DevKitC-1-N8R8-v1]
  Part1 = Adafruit I2S Mic - SPH0645 [part_number="Adafruit #3421"]

nets:
  N1: M1.pin_1, M1.pin_2, Part1.VDD
  N2: M1.pin_16, Part1.DATA
  N3: M1.pin_17, Part1.WS
  N4: M1.pin_18, Part1.BCLK
  N5: M1.pin_22, M1.pin_23, M1.pin_24, M1.pin_44, Part1.GND, Part1.SELECT

custom parts:
  ESP32-S3-DevKitC-1-N8R8-v1: ESP32-S3-DevKitC-1-N8R8-v1 This module is 44pins long (2x22) and 11 pins width.
  Adafruit I2S Mic - SPH0645: For many microcontrollers, adding audio input is easy with one of our analog microphone breakouts. But as you get to bigger and better microcontrollers and microcomputers, you'll find that you don't always have an analog input, or maybe you want to avoid the noise that can seep in with an analog mic system. Once you get past 8-bit micros, you will often find an I2S peripheral, that can take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
