# Fritzing sketch esp32s3+MAX (saved by Fritzing 0.9.3b)
breadboards: 1

parts:
  SP1 = SPEAKER [package=pcb_mount_speaker]
  Part1 = Adafruit MAX98357A I2S 3W Class D Amplifier [part_number="Adafruit #3006"]
  M1 = ESP32-S3-DevKitC-1-N8R8-v1 [part_number=ESP32-S3-DevKitC-1-N8R8-v1]

nets:
  N1: SP1.+, Part1.VO-
  N2: SP1.-, Part1.VO+
  N3: Part1.VIN, M1.pin_1, M1.pin_2
  N4: Part1.GND, M1.pin_22, M1.pin_23, M1.pin_24, M1.pin_44
  N5: Part1.DIN, M1.pin_37
  N6: Part1.BCLK, M1.pin_38
  N7: Part1.LRCLK, M1.pin_39

custom parts:
  Adafruit MAX98357A I2S 3W Class D Amplifier: Listen to this good news - we now have an all in one digital audio amp breakout board that works incredibly well with the Raspberry Pi! If you're looking for an easy and low cost way to get you digital sound files bumpin' then the MAX08357 I2S Amp Breakout is for you. It takes standard I2S digital audio input and, not only decodes it into analog, but also amplifies it directly into a speaker.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
  ESP32-S3-DevKitC-1-N8R8-v1: ESP32-S3-DevKitC-1-N8R8-v1 This module is 44pins long (2x22) and 11 pins width.
