# Fritzing sketch MPU6050 and RGB (saved by Fritzing 0.9.3b)
breadboards: 1

parts:
  M1 = ESP32-S3-DevKitC-1-N8R8-v1 [part_number=ESP32-S3-DevKitC-1-N8R8-v1]
  LED1 = RGB LED (com. cathode, rbg) [package="5 mm [THT]"]
  R1 = Resistor [tolerance=±5% resistance=220 package="0805 [SMD]"]
  R2 = Resistor [tolerance=±5% resistance=220 package="0805 [SMD]"]
  R3 = Resistor [tolerance=±5% resistance=220 package="0805 [SMD]"]
  Part1 = Adafruit I2S Mic - SPH0645 [part_number="Adafruit #3421"]

nets:
  N1: M1.pin_1, M1.pin_2, LED1.common_cathode, Part1.VDD
  N2: M1.pin_10, R1.Pin_1
  N3: M1.pin_11, R3.Pin_1
  N4: M1.pin_12, R2.Pin_1
  N5: M1.pin_16, Part1.DATA
  N6: M1.pin_17, Part1.WS
  N7: M1.pin_18, Part1.BCLK
  N8: M1.pin_22, M1.pin_23, M1.pin_24, M1.pin_44, Part1.GND, Part1.SELECT
  N9: LED1.red_anode, R2.Pin_0
  N10: LED1.blue_anode, R3.Pin_0
  N11: LED1.green_anode, R1.Pin_0

custom parts:
  ESP32-S3-DevKitC-1-N8R8-v1: ESP32-S3-DevKitC-1-N8R8-v1 This module is 44pins long (2x22) and 11 pins width.
  Adafruit I2S Mic - SPH0645: For many microcontrollers, adding audio input is easy with one of our analog microphone breakouts. But as you get to bigger and better microcontrollers and microcomputers, you'll find that you don't always have an analog input, or maybe you want to avoid the noise that can seep in with an analog mic system. Once you get past 8-bit micros, you will often find an I2S peripheral, that can take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
