# Fritzing sketch System (saved by Fritzing 0.9.3b)
breadboards: 3

parts:
  M1 = ESP32-S3-DevKitC-1-N8R8-v1 [part_number=ESP32-S3-DevKitC-1-N8R8-v1]
  LED1 = RGB LED (com. cathode, rbg) [package="5 mm [THT]"]
  R1 = Resistor [tolerance=±5% resistance=220 package="0805 [SMD]"]
  R2 = Resistor [tolerance=±5% resistance=220 package="0805 [SMD]"]
  R3 = Resistor [tolerance=±5% resistance=220 package="0805 [SMD]"]
  Part1 = Adafruit I2S Mic - SPH0645 [part_number="Adafruit #3421"]
  M2 = ESP32-S3-DevKitC-1-N8R8-v1 [part_number=ESP32-S3-DevKitC-1-N8R8-v1]
  Part2 = Adafruit MAX98357A I2S 3W Class D Amplifier [part_number="Adafruit #3006"]
  Part4 = InvenSense MPU6050
  M3 = DOIT Esp32 DevKit v1 (30 pins long, 11 pins width) [part_number=ESP32S-PIN30]
  S1 = Pushbutton [package=THT]
  SP1 = SPEAKER [package=pcb_mount_speaker]
  R4 = Resistor [tolerance=±5% resistance=1k package="0805 [SMD]"]
  R5 = Resistor [tolerance=±5% resistance=1k package="0805 [SMD]"]
  R6 = Resistor [tolerance=±5% resistance=1k package="0805 [SMD]"]
  LED3 = LED - 3mm [color="Red (633nm)" package="3 mm [THT]"]
  LED4 = LED - 3mm [color="Green (555nm)" package="3 mm [THT]"]
  LED5 = LED - 3mm [color="Blue (470nm)" package="3 mm [THT]"]
  M4 = DOIT Esp32 DevKit v1 (30 pins long, 11 pins width) [part_number=ESP32S-PIN30]

nets:
  N1: M1.pin_1, M1.pin_2, LED1.common_cathode, Part1.VDD
  N2: M1.pin_10, R1.Pin_1
  N3: M1.pin_11, R3.Pin_1
  N4: M1.pin_12, R2.Pin_1
  N5: M1.pin_16, Part1.DATA
  N6: M1.pin_17, Part1.WS
  N7: M1.pin_18, Part1.BCLK
  N8: M1.pin_22, M1.pin_23, M1.pin_24, M1.pin_44, Part1.GND, Part1.SELECT, R4.Pin_1, R5.Pin_1, R6.Pin_1
  N9: M1.pin_27, LED4.anode, M4.D27
  N10: M1.pin_40, LED5.anode, M4.D26
  N11: M1.pin_41, LED3.anode, M4.D25
  N12: LED1.red_anode, R2.Pin_0
  N13: LED1.blue_anode, R3.Pin_0
  N14: LED1.green_anode, R1.Pin_0
  N15: M2.pin_1, M2.pin_2
  N16: M2.pin_10, M4.RX2
  N17: M2.pin_11, M4.TX2
  N18: M2.pin_22, M2.pin_23, M2.pin_24, M2.pin_44
  VIN: Part2.VIN, M4.VIN
  GND: Part2.GND, M4.GND
  N19: Part2.DIN, M4.D14
  N20: Part2.BCLK, M4.D13
  N21: Part2.LRCLK, M4.D12
  N22: Part2.VO-, SP1.+
  N23: Part2.VO+, SP1.-
  VCC: Part4.VCC, M3.3V3, S1.leg0
  GND_2: Part4.GND, M3.GND
  N24: Part4.SCL, M3.D22
  N25: Part4.SDA, M3.D21
  N26: M3.D26, S1.leg1
  N27: R4.Pin_0, LED5.cathode
  N28: R5.Pin_0, LED3.cathode
  N29: R6.Pin_0, LED4.cathode

custom parts:
  ESP32-S3-DevKitC-1-N8R8-v1: ESP32-S3-DevKitC-1-N8R8-v1 This module is 44pins long (2x22) and 11 pins width.
  Adafruit I2S Mic - SPH0645: For many microcontrollers, adding audio input is easy with one of our analog microphone breakouts. But as you get to bigger and better microcontrollers and microcomputers, you'll find that you don't always have an analog input, or maybe you want to avoid the noise that can seep in with an analog mic system. Once you get past 8-bit micros, you will often find an I2S peripheral, that can take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
  Adafruit MAX98357A I2S 3W Class D Amplifier: Listen to this good news - we now have an all in one digital audio amp breakout board that works incredibly well with the Raspberry Pi! If you're looking for an easy and low cost way to get you digital sound files bumpin' then the MAX08357 I2S Amp Breakout is for you. It takes standard I2S digital audio input and, not only decodes it into analog, but also amplifies it directly into a speaker.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
  DOIT Esp32 DevKit v1 (30 pins long, 11 pins width): The DOIT Esp32 DevKit v1 is one of the development board created by DOIT to evaluate the ESP-WROOM-32 module. It is based on the ESP32 microcontroller that boasts Wifi, Bluetooth, Ethernet and Low Power support all in a single chip. (vanepp) made breadboard work, adjusted pin numbering and labels and reduced size of schematic and cleaned up pcb. This chip is 30pins long (2 x15) and 11 pins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
