# Fritzing sketch RGB Led (saved by Fritzing 0.9.3b)
breadboards: 1

parts:
  M1 = ESP32-S3-DevKitC-1-N8R8-v1 [part_number=ESP32-S3-DevKitC-1-N8R8-v1]
  LED1 = RGB LED (com. cathode, rbg) [package="5 mm [THT]"]
  R1 = Resistor [tolerance=±5% resistance=220 package="0805 [SMD]"]
  R2 = Resistor [tolerance=±5% resistance=220 package="0805 [SMD]"]
  R3 = Resistor [tolerance=±5% resistance=220 package="0805 [SMD]"]

nets:
  N1: M1.pin_1, M1.pin_2, LED1.common_cathode
  N2: M1.pin_10, R2.Pin_1
  N3: M1.pin_11, R1.Pin_1
  N4: M1.pin_12, R3.Pin_1
  N5: M1.pin_22, M1.pin_23, M1.pin_24, M1.pin_44
  N6: LED1.red_anode, R3.Pin_0
  N7: LED1.blue_anode, R1.Pin_0
  N8: LED1.green_anode, R2.Pin_0

custom parts:
  ESP32-S3-DevKitC-1-N8R8-v1: ESP32-S3-DevKitC-1-N8R8-v1 This module is 44pins long (2x22) and 11 pins width.
