# Fritzing sketch FSR402 (saved by Fritzing 0.9.3b)
breadboards: 1

parts:
  M1 = DOIT Esp32 DevKit v1 (30 pins long, 11 pins width) [part_number=ESP32S-PIN30]
  R1 = Resistor [tolerance=±5% resistance=1k package="0805 [SMD]"]
  R2 = Resistor [tolerance=±5% resistance=220 package="2512 [SMD]"]
  U1 = Vibration Motor- ROB-08449 [package=vibe-motor-10mm]
  Q1 = NPN-Transistor [package="TO92 [THT]"]

nets:
  N1: M1.VN, R2.Pin_1
  N2: M1.D26, R1.Pin_1
  N3: M1.VIN, Q1.C
  N4: R1.Pin_0, Q1.B
  N5: R2.Pin_0, U1.-
  N6: U1.+, Q1.E

custom parts:
  DOIT Esp32 DevKit v1 (30 pins long, 11 pins width): The DOIT Esp32 DevKit v1 is one of the development board created by DOIT to evaluate the ESP-WROOM-32 module. It is based on the ESP32 microcontroller that boasts Wifi, Bluetooth, Ethernet and Low Power support all in a single chip. (vanepp) made breadboard work, adjusted pin numbering and labels and reduced size of schematic and cleaned up pcb. This chip is 30pins long (2 x15) and 11 pins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
